// Logisim project BCD.circ as structural Verilog
module BCD (
  input  [3:0] in_1,
  output out_2,
  output out_3,
  output out_4,
  output out_5,
  output out_6,
  output out_7,
  output out_8
);

  wire and_1_out, and_2_out, and_3_out, and_4_out, and_5_out, and_6_out, and_7_out, and_8_out, and_9_out,
       and_10_out, and_11_out, and_12_out, xnor_1_out, xnor_2_out;

  xnor xnor_1 (xnor_1_out, in_1[2], in_1[0]);
  xnor xnor_2 (xnor_2_out, in_1[1], in_1[0]);
  and and_1 (and_1_out, ~in_1[2], ~in_1[0]);  // AND_Gate
  and and_2 (and_2_out, ~in_1[0], in_1[1]);  // AND_Gate
  and and_3 (and_3_out, ~in_1[2], in_1[1]);  // AND_Gate
  and and_4 (and_4_out, in_1[2], ~in_1[1], in_1[0]);  // AND_Gate
  and and_5 (and_5_out, in_1[1], ~in_1[0]);  // AND_Gate
  and and_6 (and_6_out, ~in_1[2], ~in_1[0]);  // AND_Gate
  and and_7 (and_7_out, ~in_1[1], in_1[2]);  // AND_Gate
  and and_8 (and_8_out, ~in_1[0], in_1[2]);  // AND_Gate
  and and_9 (and_9_out, ~in_1[1], ~in_1[0]);  // AND_Gate
  and and_10 (and_10_out, ~in_1[1], in_1[2]);  // AND_Gate
  and and_11 (and_11_out, ~in_1[0], in_1[1]);  // AND_Gate
  and and_12 (and_12_out, ~in_1[2], in_1[1]);  // AND_Gate
  or or_1 (out_2, in_1[1], in_1[3], xnor_1_out);
  or or_2 (out_4, in_1[3], in_1[2], ~in_1[1], in_1[0]);  // OR_Gate
  or or_3 (out_3, in_1[3], ~in_1[2], xnor_2_out);  // OR_Gate
  or or_4 (out_6, and_5_out, and_6_out);
  or or_5 (out_7, in_1[3], and_7_out, and_8_out, and_9_out);
  or or_6 (out_8, in_1[3], and_10_out, and_11_out, and_12_out);
  or or_7 (out_5, in_1[3], and_1_out, and_2_out, and_3_out, and_4_out);

  // Other names for the same wires on the sheet: A = out_2; B = out_3; C = out_4; D = out_5; E = out_6; F = out_7;
  //   G = out_8
endmodule

module Dig (
  input  [7:0] in_1,
  output [3:0] dig_2,
  output [3:0] dig_1,
  output [3:0] dig_0
);

  wire [7:0] divisor_1_resultado, divisor_2_resultado;
  wire [7:4] divisor_1_resto, divisor_2_resto, divisor_3_resto;

  Hex_Digit_Display hex_digit_display_1 (.value(dig_0));  // open: dp
  Hex_Digit_Display hex_digit_display_2 (.value(dig_1));  // open: dp
  Divisor divisor_1 (
    .Divisor(8'ha), .Dividendo(in_1), .Resto({divisor_1_resto, dig_2}), .Resultado(divisor_1_resultado));
  Hex_Digit_Display hex_digit_display_3 (.value(dig_2));  // open: dp
  Divisor divisor_2 (
    .Divisor(8'ha), .Dividendo(divisor_1_resultado), .Resto({divisor_2_resto, dig_1}),
    .Resultado(divisor_2_resultado));
  Divisor divisor_3 (
    .Divisor(8'ha), .Dividendo(divisor_2_resultado), .Resto({divisor_3_resto, dig_0}));  // open: Resultado

  // Other names for the same wires on the sheet: _0[3:0] = dig_0; _1[3:0] = dig_1; _2[3:0] = dig_2
endmodule
