// Logisim project Divisor.circ as structural Verilog
module Divisor (
  input  [7:0] Dividendo,
  input  [7:0] Divisor,
  output [7:0] Resultado,
  output [7:0] Resto
);

  wire lookahead_8bits_1_bit7, lookahead_8bits_2_bit7, lookahead_8bits_3_bit7, lookahead_8bits_4_bit7,
       lookahead_8bits_5_bit7, lookahead_8bits_6_bit7, lookahead_8bits_7_bit7, lookahead_8bits_8_bit7;
  wire [7:0] \lookahead_8bits_1_saída , \lookahead_8bits_2_saída , \lookahead_8bits_3_saída ,
       \lookahead_8bits_4_saída , \lookahead_8bits_5_saída , \lookahead_8bits_6_saída ,
       \lookahead_8bits_7_saída , \lookahead_8bits_8_saída , multiplexer_2_out, multiplexer_3_out,
       multiplexer_4_out;
  wire [7:1] multiplexer_1_out, multiplexer_5_out, multiplexer_6_out, multiplexer_7_out;
  wire [7:7] multiplexer_1_out_2, multiplexer_5_out_2, multiplexer_6_out_2, multiplexer_7_out_2;

  not not_1 (Resultado[7], lookahead_8bits_1_bit7);
  not not_2 (Resultado[6], lookahead_8bits_2_bit7);
  not not_3 (Resultado[5], lookahead_8bits_3_bit7);
  LookAHead_8bits lookahead_8bits_1 (
    .Entrada_A({{7{1'b0}}, Dividendo[7]}), .Entrada_B(Divisor), .\Saída (\lookahead_8bits_1_saída ),
    .subtrator(1'b1), .Bit7(lookahead_8bits_1_bit7));
  LookAHead_8bits lookahead_8bits_2 (
    .Entrada_A({multiplexer_1_out, Dividendo[6]}), .Entrada_B(Divisor), .\Saída (\lookahead_8bits_2_saída ),
    .subtrator(1'b1), .Bit7(lookahead_8bits_2_bit7));
  not not_4 (Resultado[4], lookahead_8bits_4_bit7);
  not not_5 (Resultado[3], lookahead_8bits_5_bit7);
  Multiplexer #(.width(8)) multiplexer_1 (
    .in0(\lookahead_8bits_1_saída ), .in1({{7{1'b0}}, Dividendo[7]}),
    .out({multiplexer_1_out_2[7], multiplexer_1_out}), .sel(lookahead_8bits_1_bit7));  // open: en
  Multiplexer #(.width(8)) multiplexer_2 (
    .in0(\lookahead_8bits_2_saída ), .in1({multiplexer_1_out, Dividendo[6]}), .out(multiplexer_2_out),
    .sel(lookahead_8bits_2_bit7));  // open: en
  LookAHead_8bits lookahead_8bits_3 (
    .Entrada_A({multiplexer_2_out[6:0], Dividendo[5]}), .Entrada_B(Divisor),
    .\Saída (\lookahead_8bits_3_saída ), .subtrator(1'b1), .Bit7(lookahead_8bits_3_bit7));
  Multiplexer #(.width(8)) multiplexer_3 (
    .in0(\lookahead_8bits_3_saída ), .in1({multiplexer_2_out[6:0], Dividendo[5]}), .out(multiplexer_3_out),
    .sel(lookahead_8bits_3_bit7));  // open: en
  LookAHead_8bits lookahead_8bits_4 (
    .Entrada_A({multiplexer_3_out[6:0], Dividendo[4]}), .Entrada_B(Divisor),
    .\Saída (\lookahead_8bits_4_saída ), .subtrator(1'b1), .Bit7(lookahead_8bits_4_bit7));
  LookAHead_8bits lookahead_8bits_5 (
    .Entrada_A({multiplexer_4_out[6:0], Dividendo[3]}), .Entrada_B(Divisor),
    .\Saída (\lookahead_8bits_5_saída ), .subtrator(1'b1), .Bit7(lookahead_8bits_5_bit7));
  not not_6 (Resultado[2], lookahead_8bits_6_bit7);
  not not_7 (Resultado[1], lookahead_8bits_7_bit7);
  not not_8 (Resultado[0], lookahead_8bits_8_bit7);
  Multiplexer #(.width(8)) multiplexer_4 (
    .in0(\lookahead_8bits_4_saída ), .in1({multiplexer_3_out[6:0], Dividendo[4]}), .out(multiplexer_4_out),
    .sel(lookahead_8bits_4_bit7));  // open: en
  Multiplexer #(.width(8)) multiplexer_5 (
    .in0(\lookahead_8bits_5_saída ), .in1({multiplexer_4_out[6:0], Dividendo[3]}),
    .out({multiplexer_5_out_2[7], multiplexer_5_out}), .sel(lookahead_8bits_5_bit7));  // open: en
  LookAHead_8bits lookahead_8bits_6 (
    .Entrada_A({multiplexer_5_out, Dividendo[2]}), .Entrada_B(Divisor), .\Saída (\lookahead_8bits_6_saída ),
    .subtrator(1'b1), .Bit7(lookahead_8bits_6_bit7));
  LookAHead_8bits lookahead_8bits_7 (
    .Entrada_A({multiplexer_6_out, Dividendo[1]}), .Entrada_B(Divisor), .\Saída (\lookahead_8bits_7_saída ),
    .subtrator(1'b1), .Bit7(lookahead_8bits_7_bit7));
  Multiplexer #(.width(8)) multiplexer_6 (
    .in0(\lookahead_8bits_6_saída ), .in1({multiplexer_5_out, Dividendo[2]}),
    .out({multiplexer_6_out_2[7], multiplexer_6_out}), .sel(lookahead_8bits_6_bit7));  // open: en
  Multiplexer #(.width(8)) multiplexer_7 (
    .in0(\lookahead_8bits_7_saída ), .in1({multiplexer_6_out, Dividendo[1]}),
    .out({multiplexer_7_out_2[7], multiplexer_7_out}), .sel(lookahead_8bits_7_bit7));  // open: en
  LookAHead_8bits lookahead_8bits_8 (
    .Entrada_A({multiplexer_7_out, Dividendo[0]}), .Entrada_B(Divisor), .\Saída (\lookahead_8bits_8_saída ),
    .subtrator(1'b1), .Bit7(lookahead_8bits_8_bit7));
  Multiplexer #(.width(8)) multiplexer_8 (
    .in0(\lookahead_8bits_8_saída ), .in1({multiplexer_7_out, Dividendo[0]}), .out(Resto),
    .sel(lookahead_8bits_8_bit7));  // open: en

  // Other names for the same wires on the sheet: s8 = Resultado[0]; s7 = Resultado[1]; s6 = Resultado[2];
  //   s5 = Resultado[3]; s4 = Resultado[4]; s3 = Resultado[5]; s2 = Resultado[6]; s1 = Resultado[7]
endmodule
