// Logisim project LookAhead.circ as structural Verilog
module Somador_1bit (
  input  A,
  input  B,
  input  Cin,
  output S
);

  wire xor_1_out;

  xor xor_1 (xor_1_out, Cin, B);
  xor xor_2 (S, xor_1_out, A);
endmodule

module LookAHead_8bits (
  input  [7:0] Entrada_A,
  input  [7:0] Entrada_B,
  input  subtrator,
  output [7:0] \Saída ,
  output Bit7
);

  wire and_1_out, and_2_out, and_3_out, and_4_out, and_5_out, and_6_out, and_7_out, and_8_out, and_9_out,
       and_10_out, and_11_out, and_12_out, and_13_out, and_14_out, and_15_out, and_16_out, and_17_out,
       and_18_out, and_19_out, and_20_out, and_21_out, and_22_out, and_23_out, and_24_out, and_25_out,
       and_26_out, and_27_out, and_28_out, and_29_out, and_30_out, and_31_out, and_32_out, and_33_out,
       and_34_out, and_35_out, or_1_out, or_2_out, or_3_out, or_4_out, or_5_out, or_6_out, or_7_out,
       or_8_out, or_9_out, or_10_out, or_11_out, or_12_out, or_13_out, or_14_out;
  wire [7:0] xor_1_out;

  and and_1 (and_1_out, subtrator, or_3_out, or_4_out, or_6_out, or_8_out, or_11_out, or_13_out, or_14_out);
  assign xor_1_out = Entrada_B ^ {8{subtrator}};  // XOR_Gate xor_1, 8 bits wide
  and and_2 (and_2_out, or_3_out, or_4_out, or_6_out, or_8_out, or_11_out, or_13_out, and_35_out);
  and and_3 (and_3_out, or_3_out, or_4_out, or_6_out, or_8_out, or_11_out, and_33_out);
  and and_4 (and_4_out, or_3_out, or_4_out, or_6_out, or_8_out, and_30_out);
  and and_5 (and_5_out, or_3_out, or_4_out, or_6_out, and_26_out);
  or or_1 (or_1_out, and_10_out, and_1_out, and_2_out, and_3_out, and_4_out, and_5_out, and_6_out, and_7_out);
  Somador_1bit somador_1bit_1 (.S(Bit7), .A(xor_1_out[7]), .B(Entrada_A[7]), .Cin(or_1_out));
  and and_6 (and_6_out, or_3_out, or_4_out, and_21_out);
  and and_7 (and_7_out, or_3_out, and_16_out);
  and and_8 (and_8_out, subtrator, or_4_out, or_6_out, or_8_out, or_11_out, or_13_out, or_14_out);
  and and_9 (and_9_out, or_4_out, or_6_out, or_8_out, or_11_out, or_13_out, and_35_out);
  and and_10 (and_10_out, xor_1_out[6], Entrada_A[6]);
  and and_11 (and_11_out, or_4_out, or_6_out, or_8_out, or_11_out, and_33_out);
  or or_2 (or_2_out, and_16_out, and_8_out, and_9_out, and_11_out, and_12_out, and_13_out, and_14_out);
  or or_3 (or_3_out, xor_1_out[6], Entrada_A[6]);
  and and_12 (and_12_out, or_4_out, or_6_out, or_8_out, and_30_out);
  Somador_1bit somador_1bit_2 (.S(\Saída [6]), .A(xor_1_out[6]), .B(Entrada_A[6]), .Cin(or_2_out));
  and and_13 (and_13_out, or_4_out, or_6_out, and_26_out);
  and and_14 (and_14_out, or_4_out, and_21_out);
  and and_15 (and_15_out, subtrator, or_6_out, or_8_out, or_11_out, or_13_out, or_14_out);
  and and_16 (and_16_out, xor_1_out[5], Entrada_A[5]);
  and and_17 (and_17_out, or_6_out, or_8_out, or_11_out, or_13_out, and_35_out);
  or or_4 (or_4_out, xor_1_out[5], Entrada_A[5]);
  and and_18 (and_18_out, or_6_out, or_8_out, and_30_out);
  and and_19 (and_19_out, or_6_out, or_8_out, or_11_out, and_33_out);
  or or_5 (or_5_out, and_21_out, and_15_out, and_17_out, and_19_out, and_18_out, and_20_out);
  Somador_1bit somador_1bit_3 (.S(\Saída [5]), .A(xor_1_out[5]), .B(Entrada_A[5]), .Cin(or_5_out));
  and and_20 (and_20_out, or_6_out, and_26_out);
  and and_21 (and_21_out, xor_1_out[4], Entrada_A[4]);
  and and_22 (and_22_out, subtrator, or_8_out, or_11_out, or_13_out, or_14_out);
  or or_6 (or_6_out, xor_1_out[4], Entrada_A[4]);
  and and_23 (and_23_out, or_8_out, or_11_out, and_33_out);
  and and_24 (and_24_out, or_8_out, or_11_out, or_13_out, and_35_out);
  or or_7 (or_7_out, and_26_out, and_22_out, and_24_out, and_23_out, and_25_out);
  and and_25 (and_25_out, or_8_out, and_30_out);
  Somador_1bit somador_1bit_4 (.S(\Saída [4]), .A(xor_1_out[4]), .B(Entrada_A[4]), .Cin(or_7_out));
  and and_26 (and_26_out, xor_1_out[3], Entrada_A[3]);
  and and_27 (and_27_out, subtrator, or_11_out, or_13_out, or_14_out);
  or or_8 (or_8_out, xor_1_out[3], Entrada_A[3]);
  and and_28 (and_28_out, or_11_out, or_13_out, and_35_out);
  or or_9 (or_9_out, and_30_out, and_27_out, and_28_out, and_29_out);
  Somador_1bit somador_1bit_5 (.S(\Saída [3]), .A(Entrada_A[3]), .B(xor_1_out[3]), .Cin(or_9_out));
  and and_29 (and_29_out, or_11_out, and_33_out);
  and and_30 (and_30_out, xor_1_out[2], Entrada_A[2]);
  and and_31 (and_31_out, subtrator, or_14_out, or_13_out);
  or or_10 (or_10_out, and_33_out, and_31_out, and_32_out);
  or or_11 (or_11_out, xor_1_out[2], Entrada_A[2]);
  and and_32 (and_32_out, or_13_out, and_35_out);
  Somador_1bit somador_1bit_6 (.S(\Saída [2]), .A(xor_1_out[2]), .B(Entrada_A[2]), .Cin(or_10_out));
  and and_33 (and_33_out, xor_1_out[1], Entrada_A[1]);
  and and_34 (and_34_out, subtrator, or_14_out);
  or or_12 (or_12_out, and_35_out, and_34_out);
  or or_13 (or_13_out, xor_1_out[1], Entrada_A[1]);
  Somador_1bit somador_1bit_7 (.S(\Saída [1]), .A(xor_1_out[1]), .B(Entrada_A[1]), .Cin(or_12_out));
  and and_35 (and_35_out, xor_1_out[0], Entrada_A[0]);
  or or_14 (or_14_out, xor_1_out[0], Entrada_A[0]);
  Somador_1bit somador_1bit_8 (.S(\Saída [0]), .A(xor_1_out[0]), .B(Entrada_A[0]), .Cin(subtrator));

  assign \Saída [7] = Bit7;

  // Other names for the same wires on the sheet: plus_1 = subtrator
endmodule
