// Logisim project Multiplicador.circ as structural Verilog
module Multiplicador (
  input  [3:0] A,
  input  [3:0] B,
  output [7:0] out_3
);

  wire a0b1, a0b2, a0b3, a1b0, a1b1, a1b2, a1b3, a2b0, a2b1, a2b2, a2b3, a3b0, a3b1, a3b2, a3b3, main_1_cout,
       main_2_cout, main_2_s, main_3_cout, main_3_s, main_4_cout, main_4_s, main_5_cout, main_6_cout,
       main_6_s, main_7_cout, main_7_s, main_8_cout, main_8_s, main_9_cout, main_10_cout, main_11_cout;

  and and_1 (out_3[0], A[0], B[0]);
  and and_2 (a1b0, A[1], B[0]);
  and and_3 (a2b0, A[2], B[0]);
  and and_4 (a3b0, A[3], B[0]);
  and and_5 (a0b1, A[0], B[1]);
  and and_6 (a1b1, A[1], B[1]);
  and and_7 (a2b1, A[2], B[1]);
  and and_8 (a3b1, A[3], B[1]);
  and and_9 (a0b2, A[0], B[2]);
  and and_10 (a1b2, A[1], B[2]);
  and and_11 (a2b2, A[2], B[2]);
  and and_12 (a3b2, A[3], B[2]);
  and and_13 (a0b3, A[0], B[3]);
  and and_14 (a1b3, A[1], B[3]);
  and and_15 (a2b3, A[2], B[3]);
  and and_16 (a3b3, A[3], B[3]);
  Somador_8_bits_main main_1 (.Cout(main_1_cout), .S(out_3[1]), .A(a0b1), .B(a1b0), .Cin(1'b0));
  Somador_8_bits_main main_2 (.Cout(main_2_cout), .S(main_2_s), .A(a1b1), .B(a2b0), .Cin(main_1_cout));
  Somador_8_bits_main main_3 (.Cout(main_3_cout), .S(main_3_s), .A(a2b1), .B(a3b0), .Cin(main_2_cout));
  Somador_8_bits_main main_4 (.Cout(main_4_cout), .S(main_4_s), .A(a3b1), .B(1'b0), .Cin(main_3_cout));
  Somador_8_bits_main main_5 (.Cout(main_5_cout), .S(out_3[2]), .A(a0b2), .B(main_2_s), .Cin(1'b0));
  Somador_8_bits_main main_6 (.Cout(main_6_cout), .S(main_6_s), .A(a1b2), .B(main_3_s), .Cin(main_5_cout));
  Somador_8_bits_main main_7 (.Cout(main_7_cout), .S(main_7_s), .A(a2b2), .B(main_4_s), .Cin(main_6_cout));
  Somador_8_bits_main main_8 (.Cout(main_8_cout), .S(main_8_s), .A(a3b2), .B(main_4_cout), .Cin(main_7_cout));
  Somador_8_bits_main main_9 (.Cout(main_9_cout), .S(out_3[3]), .A(a0b3), .B(main_6_s), .Cin(1'b0));
  Somador_8_bits_main main_10 (.Cout(main_10_cout), .S(out_3[4]), .A(a1b3), .B(main_7_s), .Cin(main_9_cout));
  Somador_8_bits_main main_11 (.Cout(main_11_cout), .S(out_3[5]), .A(a2b3), .B(main_8_s), .Cin(main_10_cout));
  Somador_8_bits_main main_12 (.Cout(out_3[7]), .S(out_3[6]), .A(a3b3), .B(main_8_cout), .Cin(main_11_cout));

  // Other names for the same wires on the sheet: a0b0 = out_3[0]; s1 = out_3[0]; s2 = out_3[1]; s3 = out_3[2];
  //   s4 = out_3[3]; s5 = out_3[4]; s6 = out_3[5]; s7 = out_3[6]; s8 = out_3[7]
endmodule

module nha (
  input  [3:0] in_1,
  input  [3:0] B,
  output [7:0] out_3
);

  wire a0b1, a0b2, a0b3, a1b0, a1b1, a1b2, a1b3, a2b0, a2b1, a2b2, a2b3, a3b0, a3b1, a3b2, a3b3, and_17_out,
       and_18_out, and_19_out, and_20_out, and_21_out, and_22_out, and_23_out, and_24_out, and_25_out,
       and_26_out, and_27_out, and_28_out, and_29_out, and_30_out, and_31_out, and_32_out, and_33_out,
       and_34_out, and_35_out, and_36_out, and_37_out, and_38_out, and_39_out, and_40_out, and_41_out,
       and_42_out, and_43_out, and_44_out, or_1_out, or_2_out, or_3_out, or_4_out, or_5_out, or_6_out,
       or_8_out, xor_2_out, xor_3_out, xor_4_out, xor_5_out, xor_6_out, xor_7_out, xor_9_out, xor_10_out,
       xor_11_out, xor_12_out, xor_13_out, xor_14_out, xor_16_out, xor_17_out;

  and and_1 (out_3[0], in_1[0], B[0]);
  and and_2 (a1b0, in_1[1], B[0]);
  and and_3 (a2b0, in_1[2], B[0]);
  and and_4 (a3b0, in_1[3], B[0]);
  and and_5 (a0b1, in_1[0], B[1]);
  and and_6 (a1b1, in_1[1], B[1]);
  and and_7 (a2b1, in_1[2], B[1]);
  and and_8 (a3b1, in_1[3], B[1]);
  and and_9 (a0b2, in_1[0], B[2]);
  and and_10 (a1b2, in_1[1], B[2]);
  and and_11 (a2b2, in_1[2], B[2]);
  and and_12 (a3b2, in_1[3], B[2]);
  and and_13 (a0b3, in_1[0], B[3]);
  and and_14 (a1b3, in_1[1], B[3]);
  and and_15 (a2b3, in_1[2], B[3]);
  and and_16 (a3b3, in_1[3], B[3]);
  and and_17 (and_17_out, a1b1, a2b0);
  and and_18 (and_18_out, a2b1, a3b0);
  and and_19 (and_19_out, a0b1, a1b0);
  and and_20 (and_20_out, and_19_out, a1b1);
  and and_21 (and_21_out, and_19_out, a2b0);
  or or_1 (or_1_out, and_17_out, and_20_out, and_21_out);
  and and_22 (and_22_out, or_1_out, a2b1);
  and and_23 (and_23_out, or_1_out, a3b0);
  or or_2 (or_2_out, and_18_out, and_22_out, and_23_out);
  and and_24 (and_24_out, a3b1, or_2_out);
  xor xor_1 (out_3[1], a1b0, a0b1);
  xor xor_2 (xor_2_out, and_19_out, a2b0);
  xor xor_3 (xor_3_out, or_1_out, a3b0);
  xor xor_4 (xor_4_out, or_2_out, a3b1);
  xor xor_5 (xor_5_out, xor_2_out, a1b1);
  xor xor_6 (xor_6_out, xor_3_out, a2b1);
  and and_25 (and_25_out, a1b2, xor_6_out);
  and and_26 (and_26_out, or_5_out, a2b2);
  and and_27 (and_27_out, a2b2, xor_4_out);
  or or_3 (or_3_out, and_27_out, and_26_out, and_33_out);
  and and_28 (and_28_out, a3b2, and_24_out);
  and and_29 (and_29_out, or_3_out, a3b2);
  or or_4 (or_4_out, and_28_out, and_29_out, and_34_out);
  and and_30 (and_30_out, a0b2, xor_5_out);
  and and_31 (and_31_out, and_30_out, xor_6_out);
  and and_32 (and_32_out, and_30_out, a1b2);
  or or_5 (or_5_out, and_25_out, and_32_out, and_31_out);
  and and_33 (and_33_out, or_5_out, xor_4_out);
  xor xor_7 (xor_7_out, or_3_out, and_24_out);
  and and_34 (and_34_out, or_3_out, and_24_out);
  xor xor_8 (out_3[2], xor_5_out, a0b2);
  xor xor_9 (xor_9_out, and_30_out, xor_6_out);
  xor xor_10 (xor_10_out, or_5_out, xor_4_out);
  xor xor_11 (xor_11_out, xor_10_out, a2b2);
  xor xor_12 (xor_12_out, xor_7_out, a3b2);
  xor xor_13 (xor_13_out, xor_9_out, a1b2);
  and and_35 (and_35_out, a1b3, xor_11_out);
  and and_36 (and_36_out, or_8_out, a2b3);
  and and_37 (and_37_out, a2b3, xor_12_out);
  or or_6 (or_6_out, and_37_out, and_36_out, and_44_out);
  and and_38 (and_38_out, a3b3, or_4_out);
  and and_39 (and_39_out, or_6_out, a3b3);
  and and_40 (and_40_out, or_6_out, or_4_out);
  or or_7 (out_3[7], and_38_out, and_39_out, and_40_out);
  and and_41 (and_41_out, a0b3, xor_13_out);
  and and_42 (and_42_out, and_41_out, a1b3);
  and and_43 (and_43_out, and_41_out, xor_11_out);
  or or_8 (or_8_out, and_35_out, and_42_out, and_43_out);
  and and_44 (and_44_out, or_8_out, xor_12_out);
  xor xor_14 (xor_14_out, or_6_out, or_4_out);
  xor xor_15 (out_3[3], xor_13_out, a0b3);
  xor xor_16 (xor_16_out, and_41_out, xor_11_out);
  xor xor_17 (xor_17_out, or_8_out, xor_12_out);
  xor xor_18 (out_3[5], xor_17_out, a2b3);
  xor xor_19 (out_3[6], xor_14_out, a3b3);
  xor xor_20 (out_3[4], xor_16_out, a1b3);

  // Other names for the same wires on the sheet: a0b0 = out_3[0]; s1 = out_3[0]; s2 = out_3[1]; s3 = out_3[2];
  //   s4 = out_3[3]; s5 = out_3[4]; s6 = out_3[5]; s7 = out_3[6]; s8 = out_3[7]

  // Notes on the sheet:
  //   Cout
  //   Cout
  //   Cout
  //   Cout
  //   Cout
  //   Cout
  //   Cout
  //   Cout
  //   Cout
  //   Cout
  //   Cout
  //   Cout
endmodule
