// Logisim project Raiz.circ as structural Verilog
module raiz (
  input  [7:0] Entrada,
  output [3:0] \Saída_inteira ,
  output [3:0] \Saída_decimal 
);

  wire lookahead_8bits_2_bit7, lookahead_8bits_3_bit7, lookahead_8bits_4_bit7, lookahead_8bits_5_bit7,
       lookahead_8bits_6_bit7, lookahead_8bits_7_bit7, not_1_out, not_3_out, not_5_out, not_7_out, not_9_out,
       not_11_out, sub_9bits_1_bit_8;
  wire [3:2] \lookahead_8bits_1_saída_2 ;
  wire [7:0] \lookahead_8bits_2_saída , \lookahead_8bits_3_saída , \lookahead_8bits_4_saída ,
       \lookahead_8bits_5_saída , \lookahead_8bits_6_saída , \lookahead_8bits_7_saída , multiplexer_1_out,
       multiplexer_2_out, multiplexer_4_out, multiplexer_5_out, multiplexer_6_out;
  wire [7:2] \lookahead_8bits_1_saída , multiplexer_3_out_2;
  wire [7:6] multiplexer_3_out;

  LookAHead_8bits lookahead_8bits_1 (
    .Entrada_A({{6{1'b0}}, Entrada[7:6]}), .Entrada_B({{7{1'b0}}, \Saída_inteira [3]}),
    .\Saída ({\lookahead_8bits_1_saída , \lookahead_8bits_1_saída_2 }), .subtrator(1'b1));  // open: Bit7
  not not_1 (not_1_out, 1'b0);
  LookAHead_8bits lookahead_8bits_2 (
    .Entrada_A({4'b0000, \lookahead_8bits_1_saída_2 , Entrada[5:4]}),
    .Entrada_B({{5{1'b0}}, \Saída_inteira [3], 2'b01}), .\Saída (\lookahead_8bits_2_saída ),
    .subtrator(not_1_out), .Bit7(lookahead_8bits_2_bit7));
  not not_2 (\Saída_inteira [2], lookahead_8bits_2_bit7);
  Multiplexer #(.width(8)) multiplexer_1 (
    .in0(\lookahead_8bits_2_saída ), .in1({4'b0000, \lookahead_8bits_1_saída_2 , Entrada[5:4]}),
    .out(multiplexer_1_out), .sel(lookahead_8bits_2_bit7));  // open: en
  or or_1 (\Saída_inteira [3], Entrada[6], Entrada[7]);
  LookAHead_8bits lookahead_8bits_3 (
    .Entrada_A({multiplexer_1_out[5:0], Entrada[3:2]}), .Entrada_B({4'b0000, \Saída_inteira [3:2], 2'b01}),
    .\Saída (\lookahead_8bits_3_saída ), .subtrator(not_3_out), .Bit7(lookahead_8bits_3_bit7));
  not not_3 (not_3_out, 1'b0);
  Multiplexer #(.width(8)) multiplexer_2 (
    .in0(\lookahead_8bits_3_saída ), .in1({multiplexer_1_out[5:0], Entrada[3:2]}), .out(multiplexer_2_out),
    .sel(lookahead_8bits_3_bit7));  // open: en
  not not_4 (\Saída_inteira [1], lookahead_8bits_3_bit7);
  LookAHead_8bits lookahead_8bits_4 (
    .Entrada_A({multiplexer_2_out[5:0], Entrada[1:0]}), .Entrada_B({3'b000, \Saída_inteira [3:1], 2'b01}),
    .\Saída (\lookahead_8bits_4_saída ), .subtrator(not_5_out), .Bit7(lookahead_8bits_4_bit7));
  not not_5 (not_5_out, 1'b0);
  not not_6 (\Saída_inteira [0], lookahead_8bits_4_bit7);
  Multiplexer #(.width(8)) multiplexer_3 (
    .in0(\lookahead_8bits_4_saída ), .in1({multiplexer_2_out[5:0], Entrada[1:0]}),
    .out({multiplexer_3_out, multiplexer_3_out_2}), .sel(lookahead_8bits_4_bit7));  // open: en
  LookAHead_8bits lookahead_8bits_5 (
    .Entrada_A({multiplexer_3_out_2, 2'b00}), .Entrada_B({2'b00, \Saída_inteira , 2'b01}),
    .\Saída (\lookahead_8bits_5_saída ), .subtrator(not_7_out), .Bit7(lookahead_8bits_5_bit7));
  not not_7 (not_7_out, 1'b0);
  Multiplexer #(.width(8)) multiplexer_4 (
    .in0(\lookahead_8bits_5_saída ), .in1({multiplexer_3_out_2, 2'b00}), .out(multiplexer_4_out),
    .sel(lookahead_8bits_5_bit7));  // open: en
  not not_8 (\Saída_decimal [3], lookahead_8bits_5_bit7);
  not not_9 (not_9_out, 1'b0);
  LookAHead_8bits lookahead_8bits_6 (
    .Entrada_A({multiplexer_4_out[5:0], 2'b00}),
    .Entrada_B({1'b0, \Saída_inteira , \Saída_decimal [3], 2'b01}), .\Saída (\lookahead_8bits_6_saída ),
    .subtrator(not_9_out), .Bit7(lookahead_8bits_6_bit7));
  not not_10 (\Saída_decimal [2], lookahead_8bits_6_bit7);
  Multiplexer #(.width(8)) multiplexer_5 (
    .in0(\lookahead_8bits_6_saída ), .in1({multiplexer_4_out[5:0], 2'b00}), .out(multiplexer_5_out),
    .sel(lookahead_8bits_6_bit7));  // open: en
  not not_11 (not_11_out, 1'b0);
  LookAHead_8bits lookahead_8bits_7 (
    .Entrada_A({multiplexer_5_out[5:0], 2'b00}), .Entrada_B({\Saída_inteira , \Saída_decimal [3:2], 2'b01}),
    .\Saída (\lookahead_8bits_7_saída ), .subtrator(not_11_out), .Bit7(lookahead_8bits_7_bit7));
  not not_12 (\Saída_decimal [1], lookahead_8bits_7_bit7);
  Multiplexer #(.width(8)) multiplexer_6 (
    .in0(\lookahead_8bits_7_saída ), .in1({multiplexer_5_out[5:0], 2'b00}), .out(multiplexer_6_out),
    .sel(lookahead_8bits_7_bit7));  // open: en
  sub_9bits sub_9bits_1 (
    .Entrada_A({multiplexer_6_out[6:0], 2'b00}), .Entrada_B({\Saída_inteira , \Saída_decimal [3:1], 2'b01}),
    .Bit_8(sub_9bits_1_bit_8));  // open: Cout, Saída
  not not_13 (\Saída_decimal [0], sub_9bits_1_bit_8);

  // Other names for the same wires on the sheet: b1 = Entrada[2]; b2 = Entrada[3]; b3 = Entrada[0]; b4 = Entrada[1];
  //   s8 = \Saída_decimal [0]; s7 = \Saída_decimal [1]; setimo[8:2] = {\Saída_inteira , \Saída_decimal [3:1]};
  //   s6 = \Saída_decimal [2]; sexto[7:2] = {\Saída_inteira , \Saída_decimal [3:2]};
  //   quinto[6:2] = {\Saída_inteira , \Saída_decimal [3]}; s5 = \Saída_decimal [3]; quarto[5:2] = \Saída_inteira ;
  //   s4 = \Saída_inteira [0]; s3 = \Saída_inteira [1]; terceiro[4:2] = \Saída_inteira [3:1]; s2 = \Saída_inteira [2];
  //   segundo[3:2] = \Saída_inteira [3:2]; bit = \Saída_inteira [3]; primeiro[2] = \Saída_inteira [3]
endmodule
