// Logisim project Somador 8 bits.circ as structural Verilog: 4 circuits, main circuit main
module main (
  input  A,
  input  B,
  input  Cin,
  output Cout,
  output S
);

  wire and_1_out, and_2_out, and_3_out, xor_1_out;

  and and_1 (and_1_out, A, B);
  and and_2 (and_2_out, A, Cin);
  and and_3 (and_3_out, B, Cin);
  xor xor_1 (xor_1_out, Cin, B);
  or or_1 (Cout, and_1_out, and_2_out, and_3_out);
  xor xor_2 (S, xor_1_out, A);
endmodule

module Somador_8_bits (
  input  [7:0] Entrada_B,
  input  [7:0] Entrada_A,
  input  Cin,
  output Cout,
  output [7:0] out_5
);

  wire main_1_cout, main_3_cout, main_4_cout, main_5_cout, main_6_cout, main_7_cout, main_8_cout;

  main main_1 (.Cout(main_1_cout), .S(out_5[6]), .A(Entrada_A[6]), .B(Entrada_B[6]), .Cin(main_3_cout));
  main main_2 (.Cout(Cout), .S(out_5[7]), .A(Entrada_A[7]), .B(Entrada_B[7]), .Cin(main_1_cout));
  main main_3 (.Cout(main_3_cout), .S(out_5[5]), .A(Entrada_A[5]), .B(Entrada_B[5]), .Cin(main_4_cout));
  main main_4 (.Cout(main_4_cout), .S(out_5[4]), .A(Entrada_A[4]), .B(Entrada_B[4]), .Cin(main_6_cout));
  main main_5 (.Cout(main_5_cout), .S(out_5[2]), .A(Entrada_A[2]), .B(Entrada_B[2]), .Cin(main_8_cout));
  main main_6 (.Cout(main_6_cout), .S(out_5[3]), .A(Entrada_A[3]), .B(Entrada_B[3]), .Cin(main_5_cout));
  main main_7 (.Cout(main_7_cout), .S(out_5[0]), .A(Entrada_A[0]), .B(Entrada_B[0]), .Cin(Cin));
  main main_8 (.Cout(main_8_cout), .S(out_5[1]), .A(Entrada_A[1]), .B(Entrada_B[1]), .Cin(main_7_cout));

  // Notes on the sheet:
  //   Saída
endmodule

module Somador_32_bits (
  input  [31:0] in_1,
  input  [31:0] in_2,
  output out_3,
  output [31:0] out_4
);

  wire somador_8_bits_2_cout, somador_8_bits_3_cout, somador_8_bits_4_cout;

  Somador_8_bits somador_8_bits_1 (
    .Entrada_B(in_1[31:24]), .Entrada_A(in_2[31:24]), .Cout(out_3), .out_5(out_4[31:24]),
    .Cin(somador_8_bits_2_cout));
  Somador_8_bits somador_8_bits_2 (
    .Entrada_B(in_1[23:16]), .Entrada_A(in_2[23:16]), .Cout(somador_8_bits_2_cout), .out_5(out_4[23:16]),
    .Cin(somador_8_bits_3_cout));
  Somador_8_bits somador_8_bits_3 (
    .Entrada_B(in_1[15:8]), .Entrada_A(in_2[15:8]), .Cout(somador_8_bits_3_cout), .out_5(out_4[15:8]),
    .Cin(somador_8_bits_4_cout));
  Somador_8_bits somador_8_bits_4 (
    .Entrada_B(in_1[7:0]), .Entrada_A(in_2[7:0]), .Cout(somador_8_bits_4_cout), .out_5(out_4[7:0]), .Cin(1'b0));

  // Notes on the sheet:
  //   Entrada A
  //   Entrada B
  //   Saída
endmodule

module sub_9bits (
  input  [8:0] Entrada_A,
  input  [8:0] Entrada_B,
  output Cout,
  output Bit_8,
  output [8:0] \Saída 
);

  wire main_2_cout, main_3_cout, main_4_cout, main_5_cout, main_6_cout, main_7_cout, main_8_cout, main_9_cout;
  wire [8:0] not_1_out;

  assign not_1_out = ~Entrada_B;  // NOT_Gate not_1, 9 bits wide
  main main_1 (.Cout(Cout), .S(Bit_8), .A(not_1_out[8]), .B(Entrada_A[8]), .Cin(main_2_cout));
  main main_2 (.Cout(main_2_cout), .S(\Saída [7]), .A(not_1_out[7]), .B(Entrada_A[7]), .Cin(main_3_cout));
  main main_3 (.Cout(main_3_cout), .S(\Saída [6]), .A(not_1_out[6]), .B(Entrada_A[6]), .Cin(main_4_cout));
  main main_4 (.Cout(main_4_cout), .S(\Saída [5]), .A(not_1_out[5]), .B(Entrada_A[5]), .Cin(main_5_cout));
  main main_5 (.Cout(main_5_cout), .S(\Saída [4]), .A(not_1_out[4]), .B(Entrada_A[4]), .Cin(main_6_cout));
  main main_6 (.Cout(main_6_cout), .S(\Saída [3]), .A(not_1_out[3]), .B(Entrada_A[3]), .Cin(main_7_cout));
  main main_7 (.Cout(main_7_cout), .S(\Saída [2]), .A(not_1_out[2]), .B(Entrada_A[2]), .Cin(main_8_cout));
  main main_8 (.Cout(main_8_cout), .S(\Saída [1]), .A(not_1_out[1]), .B(Entrada_A[1]), .Cin(main_9_cout));
  main main_9 (.Cout(main_9_cout), .S(\Saída [0]), .A(not_1_out[0]), .B(Entrada_A[0]), .Cin(1'b1));

  assign \Saída [8] = Bit_8;
endmodule
