// Logisim project ULA com memória.circ as structural Verilog
module computador_8_bits (
  input  \Gravação_da_memória ,
  input  [11:0] in_2
);

  wire Clock, not_1_out;
  wire [2:0] \contador0a7_1_saída ;
  wire [3:0] d1, d2, d3;
  wire [7:0] processador_1_out, \registrador_8bits_1_saída ;
  wire [11:0] and_1_out, and_2_out, \memoria_12x8_1_saída , or_1_out;

  Clock clock_1 (.out(Clock));
  assign and_1_out = in_2 & {12{\Gravação_da_memória }};  // AND_Gate and_1, 12 bits wide
  contador0a7 contador0a7_1 (.Clock(Clock), .\Saída (\contador0a7_1_saída ));
  assign and_2_out = ~{12{\Gravação_da_memória }} & \memoria_12x8_1_saída ;  // AND_Gate and_2, 12 bits wide
  assign or_1_out = and_1_out | and_2_out;  // OR_Gate or_1, 12 bits wide
  Memoria_12x8 memoria_12x8_1 (
    .Entrada(or_1_out), .\Endereço (\contador0a7_1_saída ), .Leitura_Escrita(Clock),
    .\Saída (\memoria_12x8_1_saída ));
  // Probe on \contador0a7_1_saída 
  // Probe on \memoria_12x8_1_saída 
  Processador processador_1 (
    .Out(processador_1_out), .op_code(\memoria_12x8_1_saída [11:8]), .A(\memoria_12x8_1_saída [7:0]),
    .B(\registrador_8bits_1_saída ));
  not not_1 (not_1_out, Clock);
  Hex_Digit_Display hex_digit_display_1 (.value(d1));  // open: dp
  Hex_Digit_Display hex_digit_display_2 (.value(d2));  // open: dp
  Registrador_8bits registrador_8bits_1 (
    .Entrada(processador_1_out), .Leitura_escrita(not_1_out), .\Saída (\registrador_8bits_1_saída ));
  // Probe on \registrador_8bits_1_saída 
  Hex_Digit_Display hex_digit_display_3 (.value(d3));  // open: dp
  Dig dig_1 (.in_1(\registrador_8bits_1_saída ), .dig_2(d3), .dig_1(d2), .dig_0(d1));
endmodule

module Mux_4_bits (
  input  [3:0] entrada,
  output out_2,
  output out_3,
  output out_4,
  output out_5,
  output out_6,
  output out_7,
  output out_8,
  output out_9,
  output out_10,
  output out_11,
  output out_12,
  output out_13,
  output out_14,
  output out_15,
  output out_16,
  output out_17
);

  and and_1 (out_2, ~entrada[0], ~entrada[1], ~entrada[2], ~entrada[3]);  // AND_Gate
  and and_2 (out_3, entrada[0], ~entrada[1], ~entrada[2], ~entrada[3]);  // AND_Gate
  and and_3 (out_4, ~entrada[0], entrada[1], ~entrada[2], ~entrada[3]);  // AND_Gate
  and and_4 (out_5, entrada[0], entrada[1], ~entrada[2], ~entrada[3]);  // AND_Gate
  and and_5 (out_6, ~entrada[0], ~entrada[1], entrada[2], ~entrada[3]);  // AND_Gate
  and and_6 (out_7, entrada[0], ~entrada[1], entrada[2], ~entrada[3]);  // AND_Gate
  and and_7 (out_8, ~entrada[0], entrada[1], entrada[2], ~entrada[3]);  // AND_Gate
  and and_8 (out_9, entrada[0], entrada[1], entrada[2], ~entrada[3]);  // AND_Gate
  and and_9 (out_10, ~entrada[0], ~entrada[1], ~entrada[2], entrada[3]);  // AND_Gate
  and and_10 (out_11, entrada[0], ~entrada[1], ~entrada[2], entrada[3]);  // AND_Gate
  and and_11 (out_12, ~entrada[0], entrada[1], ~entrada[2], entrada[3]);  // AND_Gate
  and and_12 (out_13, entrada[0], entrada[1], ~entrada[2], entrada[3]);  // AND_Gate
  and and_13 (out_14, ~entrada[0], ~entrada[1], entrada[2], entrada[3]);  // AND_Gate
  and and_14 (out_15, entrada[0], ~entrada[1], entrada[2], entrada[3]);  // AND_Gate
  and and_15 (out_16, ~entrada[0], entrada[1], entrada[2], entrada[3]);  // AND_Gate
  and and_16 (out_17, entrada[0], entrada[1], entrada[2], entrada[3]);
endmodule

module \ULA_com_memória  (
  input  \Gravação_da_memória ,
  input  [11:0] in_2
);

  wire Clock, not_1_out;
  wire [2:0] \contador0a7_1_saída ;
  wire [3:0] d1, d2, d3;
  wire [7:0] processador_1_out, \registrador_8bits_1_saída ;
  wire [11:0] and_1_out, and_2_out, \memoria_12x8_1_saída , or_1_out;

  Clock clock_1 (.out(Clock));
  assign and_1_out = in_2 & {12{\Gravação_da_memória }};  // AND_Gate and_1, 12 bits wide
  contador0a7 contador0a7_1 (.Clock(Clock), .\Saída (\contador0a7_1_saída ));
  assign and_2_out = ~{12{\Gravação_da_memória }} & \memoria_12x8_1_saída ;  // AND_Gate and_2, 12 bits wide
  assign or_1_out = and_1_out | and_2_out;  // OR_Gate or_1, 12 bits wide
  Memoria_12x8 memoria_12x8_1 (
    .Entrada(or_1_out), .\Endereço (\contador0a7_1_saída ), .Leitura_Escrita(Clock),
    .\Saída (\memoria_12x8_1_saída ));
  // Probe on \contador0a7_1_saída 
  // Probe on \memoria_12x8_1_saída 
  Processador processador_1 (
    .Out(processador_1_out), .op_code(\memoria_12x8_1_saída [11:8]), .A(\memoria_12x8_1_saída [7:0]),
    .B(\registrador_8bits_1_saída ));
  not not_1 (not_1_out, Clock);
  Hex_Digit_Display hex_digit_display_1 (.value(d1));  // open: dp
  Registrador_8bits registrador_8bits_1 (
    .Entrada(processador_1_out), .Leitura_escrita(not_1_out), .\Saída (\registrador_8bits_1_saída ));
  // Probe on \registrador_8bits_1_saída 
  Hex_Digit_Display hex_digit_display_2 (.value(d2));  // open: dp
  Hex_Digit_Display hex_digit_display_3 (.value(d3));  // open: dp
  Dig dig_1 (.in_1(\registrador_8bits_1_saída ), .dig_2(d3), .dig_1(d2), .dig_0(d1));
endmodule
