// Logisim project processador 8 bits.circ as structural Verilog
module Processador (
  input  [7:0] A,
  input  [7:0] B,
  input  [3:0] op_code,
  output [7:0] Out
);

  wire [3:0] \raiz_1_saída_decimal , \raiz_1_saída_inteira , \raiz_2_saída_decimal , \raiz_2_saída_inteira ;
  wire [7:0] and_1_out, and_2_out, and_3_out, and_4_out, and_5_out, and_6_out, and_7_out, and_8_out,
       and_9_out, and_10_out, and_11_out, and_12_out, divisor_1_resultado, divisor_2_resultado,
       \lookahead_8bits_1_saída , multiplexador_1_out_2, multiplexador_1_out_3, multiplexador_1_out_4,
       multiplexador_1_out_5, multiplexador_1_out_6, multiplexador_1_out_7, multiplexador_1_out_8,
       multiplexador_1_out_9, multiplexador_1_out_10, multiplexador_1_out_11, multiplexador_1_out_12,
       multiplicador_1_out_3, not_1_out, not_2_out, or_1_out, xor_1_out;

  assign not_1_out = ~multiplexador_1_out_6;  // NOT_Gate not_1, 8 bits wide
  assign or_1_out = B | A;  // OR_Gate or_1, 8 bits wide
  assign and_1_out = B & A;  // AND_Gate and_1, 8 bits wide
  assign not_2_out = ~A;  // NOT_Gate not_2, 8 bits wide
  assign xor_1_out = B ^ A;  // XOR_Gate xor_1, 8 bits wide
  LookAHead_8bits lookahead_8bits_1 (
    .Entrada_A(B), .Entrada_B(A), .\Saída (\lookahead_8bits_1_saída ), .subtrator(not_1_out[0]));  // open: Bit7
  Multiplicador multiplicador_1 (.out_3(multiplicador_1_out_3), .A(A[3:0]), .B(B[3:0]));
  Divisor divisor_1 (.Divisor(B), .Dividendo(A), .Resultado(divisor_1_resultado));  // open: Resto
  Divisor divisor_2 (.Divisor(A), .Dividendo(B), .Resultado(divisor_2_resultado));  // open: Resto
  raiz raiz_1 (.\Saída_inteira (\raiz_1_saída_inteira ), .\Saída_decimal (\raiz_1_saída_decimal ), .Entrada(A));
  raiz raiz_2 (.\Saída_inteira (\raiz_2_saída_inteira ), .\Saída_decimal (\raiz_2_saída_decimal ), .Entrada(B));
  multiplexador multiplexador_1 (
    .in_1(op_code), .out_2(multiplexador_1_out_2), .out_3(multiplexador_1_out_3),
    .out_4(multiplexador_1_out_4), .out_5(multiplexador_1_out_5), .out_6(multiplexador_1_out_6),
    .out_7(multiplexador_1_out_7), .out_8(multiplexador_1_out_8), .out_9(multiplexador_1_out_9),
    .out_10(multiplexador_1_out_10), .out_11(multiplexador_1_out_11), .out_12(multiplexador_1_out_12));  // open: out_13
  assign and_2_out = multiplexador_1_out_2 & or_1_out;  // AND_Gate and_2, 8 bits wide
  assign and_3_out = multiplexador_1_out_3 & and_1_out;  // AND_Gate and_3, 8 bits wide
  assign and_4_out = multiplexador_1_out_4 & not_2_out;  // AND_Gate and_4, 8 bits wide
  assign and_5_out = multiplexador_1_out_5 & xor_1_out;  // AND_Gate and_5, 8 bits wide
  assign and_6_out = multiplexador_1_out_6 & \lookahead_8bits_1_saída ;  // AND_Gate and_6, 8 bits wide
  assign and_7_out = multiplexador_1_out_7 & \lookahead_8bits_1_saída ;  // AND_Gate and_7, 8 bits wide
  assign and_8_out = multiplexador_1_out_8 & multiplicador_1_out_3;  // AND_Gate and_8, 8 bits wide
  assign and_9_out = multiplexador_1_out_9 & divisor_1_resultado;  // AND_Gate and_9, 8 bits wide
  assign and_10_out = multiplexador_1_out_10 & divisor_2_resultado;  // AND_Gate and_10, 8 bits wide
  assign and_11_out = multiplexador_1_out_11 & {\raiz_1_saída_inteira , \raiz_1_saída_decimal };  // AND_Gate and_11, 8 bits wide
  assign and_12_out = multiplexador_1_out_12 & {\raiz_2_saída_inteira , \raiz_2_saída_decimal };  // AND_Gate and_12, 8 bits wide
  assign Out = and_2_out | and_3_out | and_4_out | and_5_out | and_6_out | and_10_out | and_7_out | and_8_out | and_9_out | and_11_out | and_12_out;  // OR_Gate or_2, 8 bits wide

  // Notes on the sheet:
  //   0000 - OR
  //   0001 - AND
  //   0010 - NOT
  //   0011 - XOR
  //   0100 - SOMA
  //   0101 - SUBTRAÇÃO
  //   0110 - MULTIPLICAÇÃO
  //   0111 - DIVISÃO A/B
  //   1000 - DIVISÃO B/A
  //   1001 - RAIZ (A)
  //   1010 - RAIZ (B)
  //   obs: na RAIZ os 4 bits mais significativos
  //   representam a parte inteira do resultado
  //   e os 4 bits menos significativos representam
  //   a parte decimal, que é extremamente imprecisa
endmodule

module multiplexador (
  input  [3:0] in_1,
  output [7:0] out_2,
  output [7:0] out_3,
  output [7:0] out_4,
  output [7:0] out_5,
  output [7:0] out_6,
  output [7:0] out_7,
  output [7:0] out_8,
  output [7:0] out_9,
  output [7:0] out_10,
  output [7:0] out_11,
  output [7:0] out_12,
  output [7:0] out_13
);

  and and_1 (out_2[7], ~in_1[0], ~in_1[1], ~in_1[2], ~in_1[3]);  // AND_Gate
  and and_2 (out_3[7], in_1[0], ~in_1[1], ~in_1[2], ~in_1[3]);  // AND_Gate
  and and_3 (out_4[7], ~in_1[0], in_1[1], ~in_1[2], ~in_1[3]);  // AND_Gate
  and and_4 (out_5[7], in_1[0], in_1[1], ~in_1[2], ~in_1[3]);  // AND_Gate
  and and_5 (out_6[7], ~in_1[0], ~in_1[1], in_1[2], ~in_1[3]);  // AND_Gate
  and and_6 (out_7[7], in_1[0], ~in_1[1], in_1[2], ~in_1[3]);  // AND_Gate
  and and_7 (out_8[7], ~in_1[0], in_1[1], in_1[2], ~in_1[3]);  // AND_Gate
  and and_8 (out_9[7], in_1[0], in_1[1], in_1[2], ~in_1[3]);  // AND_Gate
  and and_9 (out_10[7], ~in_1[0], ~in_1[1], ~in_1[2], in_1[3]);  // AND_Gate
  and and_10 (out_11[7], in_1[0], ~in_1[1], ~in_1[2], in_1[3]);  // AND_Gate
  and and_11 (out_12[7], ~in_1[0], in_1[1], ~in_1[2], in_1[3]);  // AND_Gate
  and and_12 (out_13[7], in_1[0], ~in_1[1], ~in_1[2], in_1[3]);  // AND_Gate

  assign out_2[6:0] = {7{out_2[7]}};
  assign out_3[6:0] = {7{out_3[7]}};
  assign out_4[6:0] = {7{out_4[7]}};
  assign out_5[6:0] = {7{out_5[7]}};
  assign out_6[6:0] = {7{out_6[7]}};
  assign out_7[6:0] = {7{out_7[7]}};
  assign out_8[6:0] = {7{out_8[7]}};
  assign out_9[6:0] = {7{out_9[7]}};
  assign out_10[6:0] = {7{out_10[7]}};
  assign out_11[6:0] = {7{out_11[7]}};
  assign out_12[6:0] = {7{out_12[7]}};
  assign out_13[6:0] = {7{out_13[7]}};
endmodule
